# Fritzing sketch densimetre (saved by Fritzing 1.0.1rc)
breadboards: 1

parts:
  A1 = Esp32-c3 super mini
  D1 = Schottky Diode [part_number=1N5817 package="300 mil [THT]"]
  V2 = DC Power [voltage=4.2V]
  DS1 = DS18B20 1-Wire Temperature Sensor [part_number=DS18B20]

nets:
  N1: A1.Pin_9, DS1.VDD
  N2: A1.Pin_10, A1.Pin_11, DS1.DQ
  N3: A1.Pin_12, DS1.GND
  N4: A1.Pin_14, D1.cathode
  GND: A1.Pin_15, V2.V-
  N5: D1.anode, V2.V+

notes:
  zf240418.1635
  manque l'accéléromètre !

custom parts:
  Esp32-c3 super mini: ESP32-C3 Development Board ESP32 SuperMini Development Board ESP32 Development Board WiFi Bluetooth.
